# Fritzing sketch Controlling LED by Potentiometer (saved by Fritzing 0.9.2b)
breadboards: 1

parts:
  LED_RED = LED - 5mm [color="Red (633nm)" package="5 mm [THT]"]
  R2 = Rotary Potentiometer (Small) [maximum_resistance=100kΩ package=THT]
  元件1 = SunFounder Uno R3
  R1 = Resistor [tolerance=±5% resistance=220 package=THT]

nets:
  N1: LED_RED.cathode, R2.leg2, 元件1.GND
  N2: LED_RED.anode, R1.Pin_0
  N3: R2.leg1, 元件1.5V
  N4: R2.wiper, 元件1.A0
  N5: 元件1.D9_PWM, R1.Pin_1

custom parts:
  SunFounder Uno R3: The SunFounder Uno is a microcontroller board based on the ATmega328 (datasheet). It has 14 digital input/output pins (of which 6 can be used as PWM outputs), 6 analog inputs, a 16 MHz ceramic resonator, a USB connection, a power jack, an ICSP header, and a reset button. It contains everything needed to support the microcontroller; simply connect it to a computer with a USB cable or power it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
