# Fritzing sketch RGB LED (saved by Fritzing 0.9.2b)
breadboards: 1

parts:
  LED1 = RGB LED (com. anode, rbg) [package="5 mm [THT]"]
  元件1 = SunFounder Uno R3
  R2 = Resistor [tolerance=±5% resistance=220 package=THT]
  R3 = Resistor [tolerance=±5% resistance=220 package=THT]
  R1 = Resistor [tolerance=±5% resistance=220 package=THT]

nets:
  N1: LED1.red_cathode, R1.Pin_1
  N2: LED1.common_anode, 元件1.GND
  N3: LED1.blue_cathode, R3.Pin_1
  N4: LED1.green_cathode, R2.Pin_1
  N5: 元件1.D9_PWM, R2.Pin_0
  N6: 元件1.D10_PWM/SS, R3.Pin_0
  N7: 元件1.D11_PWM/MOSI, R1.Pin_0

custom parts:
  SunFounder Uno R3: The SunFounder Uno is a microcontroller board based on the ATmega328 (datasheet). It has 14 digital input/output pins (of which 6 can be used as PWM outputs), 6 analog inputs, a 16 MHz ceramic resonator, a USB connection, a power jack, an ICSP header, and a reset button. It contains everything needed to support the microcontroller; simply connect it to a computer with a USB cable or power it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
