# Fritzing sketch LCD1602 (saved by Fritzing 0.9.2b)
breadboards: 1

parts:
  R4 = Rotary Potentiometer (Small) [maximum_resistance=100kΩ package=THT]
  元件1 = SunFounder Uno R3
  LCD1 = LCD screen

nets:
  5V: R4.leg1, 元件1.5V, LCD1.VDD
  N1: R4.wiper, LCD1.V0
  GND: R4.leg2, 元件1.GND, LCD1.VSS, LCD1.R/W, LCD1.LED-
  N2: 元件1.D10_PWM/SS, LCD1.DB4
  N3: 元件1.D11_PWM/MOSI, LCD1.DB5
  N4: 元件1.D12/MISO, LCD1.DB6
  N5: 元件1.D13/SCK, LCD1.DB7
  N6: 元件1.D4, LCD1.RS
  N7: 元件1.D6_PWM, LCD1.E
  N8: 元件1.3V3, LCD1.LED+

custom parts:
  SunFounder Uno R3: The SunFounder Uno is a microcontroller board based on the ATmega328 (datasheet). It has 14 digital input/output pins (of which 6 can be used as PWM outputs), 6 analog inputs, a 16 MHz ceramic resonator, a USB connection, a power jack, an ICSP header, and a reset button. It contains everything needed to support the microcontroller; simply connect it to a computer with a USB cable or power it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
