# Fritzing sketch 7-Segment Display (saved by Fritzing 0.9.2b)
breadboards: 1

parts:
  DI1 = 7-Segment LED Display [package=THT]
  元件1 = SunFounder Uno R3
  R7 = Resistor [tolerance=±5% resistance=220 package=THT]
  R8 = Resistor [tolerance=±5% resistance=220 package=THT]
  R6 = Resistor [tolerance=±5% resistance=220 package=THT]
  R5 = Resistor [tolerance=±5% resistance=220 package=THT]
  R4 = Resistor [tolerance=±5% resistance=220 package=THT]
  R3 = Resistor [tolerance=±5% resistance=220 package=THT]
  R2 = Resistor [tolerance=±5% resistance=220 package=THT]
  R1 = Resistor [tolerance=±5% resistance=220 package=THT]

nets:
  N1: DI1.cathodeE, R6.Pin_1
  N2: DI1.cathodeD, R5.Pin_1
  N3: DI1.commAnode#2, 元件1.GND
  N4: DI1.cathodeC, R8.Pin_0
  N5: DI1.cathodeDP, R7.Pin_0
  N6: DI1.cathodeB, R1.Pin_0
  N7: DI1.cathodeA, R2.Pin_0
  N8: DI1.cathodeF, R3.Pin_1
  N9: DI1.cathodeG, R4.Pin_1
  N10: 元件1.D8, R3.Pin_0
  N11: 元件1.D9_PWM, R4.Pin_0
  N12: 元件1.D10_PWM/SS, R6.Pin_0
  N13: 元件1.D11_PWM/MOSI, R5.Pin_0
  N14: 元件1.D4, R7.Pin_1
  N15: 元件1.D5_PWM, R8.Pin_1
  N16: 元件1.D6_PWM, R1.Pin_1
  N17: 元件1.D7, R2.Pin_1

custom parts:
  SunFounder Uno R3: The SunFounder Uno is a microcontroller board based on the ATmega328 (datasheet). It has 14 digital input/output pins (of which 6 can be used as PWM outputs), 6 analog inputs, a 16 MHz ceramic resonator, a USB connection, a power jack, an ICSP header, and a reset button. It contains everything needed to support the microcontroller; simply connect it to a computer with a USB cable or power it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
