# Fritzing sketch Dot-matrix (saved by Fritzing 0.9.2b)
breadboards: 1

parts:
  U1 = 74HC595 SMD [package="SO16 [SMD]"]
  U2 = 74HC595 [package="DIP16 [THT]"]
  module1 = 788BS Dot matix
  元件1 = SunFounder Uno R3
  R7 = Resistor [tolerance=±5% resistance=220 package=THT]
  R6 = Resistor [tolerance=±5% resistance=220 package=THT]
  R1 = Resistor [tolerance=±5% resistance=220 package=THT]
  R4 = Resistor [tolerance=±5% resistance=220 package=THT]
  R3 = Resistor [tolerance=±5% resistance=220 package=THT]
  R2 = Resistor [tolerance=±5% resistance=220 package=THT]
  R5 = Resistor [tolerance=±5% resistance=220 package=THT]
  R8 = Resistor [tolerance=±5% resistance=220 package=THT]

nets:
  N1: U1.Q1, R6.Pin_1
  N2: U1.Q2, R1.Pin_1
  N3: U1.Q3, R4.Pin_1
  N4: U1.Q4, R3.Pin_1
  N5: U1.Q5, R2.Pin_1
  N6: U1.Q6, R5.Pin_1
  N7: U1.Q7, R8.Pin_1
  GND: U1.GND, U1.OE, U2.GND, U2.OE, 元件1.GND
  VCC: U1.MR, U1.VCC, U2.MR, U2.VCC, 元件1.5V
  N8: U1.SH_CP, U2.SH_CP, 元件1.D12/MISO
  N9: U1.ST_CP, U2.ST_CP, 元件1.D8
  N10: U1.DS, U2.Q7'
  N11: U1.Q0, R7.Pin_1
  N12: U2.Q1, module1.P3
  N13: U2.Q2, module1.P4
  N14: U2.Q3, module1.P10
  N15: U2.Q4, module1.P6
  N16: U2.Q5, module1.P11
  N17: U2.Q6, module1.P15
  N18: U2.Q7, module1.P16
  N19: U2.DS, 元件1.D11_PWM/MOSI
  N20: U2.Q0, module1.P13
  N21: module1.P1, R4.Pin_0
  N22: module1.P2, R6.Pin_0
  N23: module1.P5, R7.Pin_0
  N24: module1.P7, R1.Pin_0
  N25: module1.P8, R2.Pin_0
  N26: module1.P9, R8.Pin_0
  N27: module1.P12, R3.Pin_0
  N28: module1.P14, R5.Pin_0

custom parts:
  788BS Dot matix: 788BS 8x8 dot matix from SunFounder
  SunFounder Uno R3: The SunFounder Uno is a microcontroller board based on the ATmega328 (datasheet). It has 14 digital input/output pins (of which 6 can be used as PWM outputs), 6 analog inputs, a 16 MHz ceramic resonator, a USB connection, a power jack, an ICSP header, and a reset button. It contains everything needed to support the microcontroller; simply connect it to a computer with a USB cable or power it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
