# Fritzing sketch ne555 (saved by Fritzing 0.9.2b)
breadboards: 1

parts:
  NE555 = General purpose bipolar Timer [package=dil-08]
  part = Ceramic Capacitor [capacitance=100nF package="100 mil [THT, multilayer]"]
  R1 = Rotary Potentiometer (Small) [maximum_resistance=100kΩ package=THT]
  R2 = Resistor [tolerance=±5% resistance=10k package=THT]
  part_2 = Ceramic Capacitor [capacitance=100nF package="100 mil [THT, multilayer]"]
  元件2 = SunFounder Uno R3

nets:
  GND: NE555.GND, part.0, part_2.1, 元件2.GND
  N1: NE555.TRI, NE555.TRE, part.1, R1.leg1
  N2: NE555.OUT, 元件2.D7
  N3: NE555._RES, NE555.VCC+, R2.Pin_0, 元件2.5V
  N4: NE555.CON, part_2.0
  N5: NE555.DIS, R1.wiper, R2.Pin_1

custom parts:
  SunFounder Uno R3: The SunFounder Uno is a microcontroller board based on the ATmega328 (datasheet). It has 14 digital input/output pins (of which 6 can be used as PWM outputs), 6 analog inputs, a 16 MHz ceramic resonator, a USB connection, a power jack, an ICSP header, and a reset button. It contains everything needed to support the microcontroller; simply connect it to a computer with a USB cable or power it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
