# Fritzing sketch ADXL345 (saved by Fritzing 0.8.7b)
breadboards: 1

parts:
  元件4 = SunFounder Uno R3
  3-axis_accelerometer1 = ADXL345 [package=THT]

nets:
  N1: 元件4.A4/SDA, 3-axis_accelerometer1.SDA
  N2: 元件4.A5/SCL, 3-axis_accelerometer1.SCL
  3V3: 元件4.3V3, 3-axis_accelerometer1.3.3V
  GND: 元件4.GND, 3-axis_accelerometer1.GND

custom parts:
  SunFounder Uno R3: The SunFounder Uno is a microcontroller board based on the ATmega328 (datasheet). It has 14 digital input/output pins (of which 6 can be used as PWM outputs), 6 analog inputs, a 16 MHz ceramic resonator, a USB connection, a power jack, an ICSP header, and a reset button. It contains everything needed to support the microcontroller; simply connect it to a computer with a USB cable or power it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
  ADXL345: An ADXL345 is a small, thin, low power, 3-axis accelerometer with high resolution (13-bit) measurement at up to ±16 g. Digital output data is formatted as 16-bit two’s complement and is accessible through either an SPI (3- or 4-wire) or I2C digital interface.
