# Fritzing sketch Simple Creation - Traffic Light (saved by Fritzing 0.8.7b)
breadboards: 1

parts:
  元件1 = SunFounder Uno R3
  module1 = Rotary Encoder v1.0
  R1 = Resistor [tolerance=±5% resistance=220 package=THT]
  R2 = Resistor [tolerance=±5% resistance=220 package=THT]
  R3 = Resistor [tolerance=±5% resistance=220 package=THT]
  LED1 = LED - 5mm [color="Yellow (592nm)" package="5 mm [THT]"]
  LED2 = LED - 5mm [color="Red (633nm)" package="5 mm [THT]"]
  LED3 = LED - 5mm [color="Green (565nm)" package="5 mm [THT]"]

nets:
  N1: 元件1.D8, R2.Pin_1
  N2: 元件1.D9_PWM, R3.Pin_1
  GND: 元件1.GND, module1.GND, LED1.cathode, LED2.cathode, LED3.cathode
  N3: 元件1.D2, module1.CLK
  N4: 元件1.D3_PWM, module1.DT
  N5: 元件1.D6_PWM, module1.SW
  N6: 元件1.D7, R1.Pin_1
  5V: 元件1.5V, module1.VCC
  N7: R1.Pin_0, LED2.anode
  N8: R2.Pin_0, LED1.anode
  N9: R3.Pin_0, LED3.anode

notes:
  Rotary encoder

custom parts:
  SunFounder Uno R3: The SunFounder Uno is a microcontroller board based on the ATmega328 (datasheet). It has 14 digital input/output pins (of which 6 can be used as PWM outputs), 6 analog inputs, a 16 MHz ceramic resonator, a USB connection, a power jack, an ICSP header, and a reset button. It contains everything needed to support the microcontroller; simply connect it to a computer with a USB cable or power it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
  Rotary Encoder v1.0: Rotary Encoder module of SunFounder Sensor Kit
