# Fritzing sketch Small Fan_simple (saved by Fritzing 0.8.7b)
circuit board: 8.46667cm x 5.64444cm
breadboards: 1

parts:
  IC1 = L293D [package=THT]
  M1 = DC Motor
  S2 = Pushbutton [package="[THT]"]
  R6 = Resistor [tolerance=±5% resistance=10k package=THT]
  元件1 = SunFounder Uno R3
  C1 = Ceramic Capacitor [capacitance=100nF package="100 mil [THT, multilayer]"]

nets:
  N1: IC1.Enable_1, IC1.+Vmotor, IC1.+V, S2.Pin_1, S2.Pin_2, 元件1.5V
  N2: IC1.In_1, 元件1.D10_PWM/SS
  N3: IC1.Out_1_(_Controlled_by_Enable_1_), M1.pin_2
  N4: IC1.0V, R6.Pin_0, 元件1.GND, C1.0
  N5: IC1.Out_2_(_Controlled_by_Enable_1_), M1.pin_1
  N6: IC1.In_2, 元件1.D9_PWM
  N7: S2.Pin_3, S2.Pin_4, R6.Pin_1, 元件1.D2, C1.1

custom parts:
  SunFounder Uno R3: The SunFounder Uno is a microcontroller board based on the ATmega328 (datasheet). It has 14 digital input/output pins (of which 6 can be used as PWM outputs), 6 analog inputs, a 16 MHz ceramic resonator, a USB connection, a power jack, an ICSP header, and a reset button. It contains everything needed to support the microcontroller; simply connect it to a computer with a USB cable or power it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
